# Fritzing sketch GUARDIAN (saved by Fritzing 0.9.10b)

parts:
  Parça1 = RFID-RC522 [part_number=101218]
  Parça2 = Arduino Uno (Rev3)
  J1 = Basic Servo
  SIM800L_BO2 = SIM800L BO
  Grove1 = Grove OLED 128x96
  Power_plug1 = Power plug

nets:
  N1: Parça1.SDA, Parça2.D10_PWM/SS
  N2: Parça1.SCK, Parça2.D13/SCK
  N3: Parça1.MOSI, Parça2.D11_PWM/MOSI, J1.pulse
  N4: Parça1.MISO, Parça2.D12/MISO
  N5: Parça1.RST, Parça2.D9_PWM
  3.3V: Parça1.3.3V, Parça2.3V3
  GND: Parça2.GND, J1.gnd, SIM800L_BO2.pin_5, Power_plug1.GND
  N6: Parça2.A4/SDA, Grove1.SDA
  N7: Parça2.A5/SCL, Grove1.SCL
  N8: Parça2.D0/RX, SIM800L_BO2.pin_10
  N9: Parça2.D1/TX, SIM800L_BO2.pin_12
  VIN: Parça2.VIN, Power_plug1.VCC

notes:
  VCC=3.3 V
  GND=GND
  RST=RESET=9.PIN
  MISO=MASTER IN SLAVE OUT=12.PIN
  MOSI=MASTER OUT SLAVE IN=11.PIN
  SCK=SERIAL CLOCK=13.PIN
  SDA=SERIALDATA=10.PIN
  .
  TXD of 800l
  RXD of 800l
  5V ,2Amp Power Supply
